// Logisim project addition.circ as structural Verilog: 4 circuits, main circuit ha
module ha (
  input  Ai,
  input  Bi,
  output Sum,
  output Carry
);

  xor xor_1 (Sum, Ai, Bi);
  and and_1 (Carry, Bi, Ai);
endmodule

module ripple_adder (
  input  A3,
  input  A2,
  input  A1,
  input  A0,
  input  B3,
  input  B2,
  input  B1,
  input  B0,
  output Carry_out,
  output D3,
  output D2,
  output D1,
  output D0
);

  wire full_adder_by_half_adder_2_carry, full_adder_by_half_adder_3_carry, ha_1_carry;

  full_adder_by_half_adder full_adder_by_half_adder_1 (
    .Ai(full_adder_by_half_adder_2_carry), .Bi(B3), .Carry_in(A3), .Sum(D3), .Carry(Carry_out));
  full_adder_by_half_adder full_adder_by_half_adder_2 (
    .Ai(full_adder_by_half_adder_3_carry), .Bi(B2), .Carry_in(A2), .Sum(D2),
    .Carry(full_adder_by_half_adder_2_carry));
  ha ha_1 (.Sum(D0), .Carry(ha_1_carry), .Ai(A0), .Bi(B0));
  full_adder_by_half_adder full_adder_by_half_adder_3 (
    .Ai(ha_1_carry), .Bi(B1), .Carry_in(A1), .Sum(D1), .Carry(full_adder_by_half_adder_3_carry));
endmodule

module full_adder (
  input  Ai,
  input  Bi,
  input  in_3,
  output Sum,
  output Carry
);

  wire and_1_out, and_2_out, or_1_out, xor_1_out;

  xor xor_1 (xor_1_out, Bi, Ai);
  or or_1 (or_1_out, Bi, Ai);
  xor xor_2 (Sum, xor_1_out, in_3);
  and and_1 (and_1_out, or_1_out, in_3);
  and and_2 (and_2_out, Bi, Ai);
  or or_2 (Carry, and_1_out, and_2_out);
endmodule

module full_adder_by_half_adder (
  input  Ai,
  input  Bi,
  input  Carry_in,
  output Sum,
  output Carry
);

  wire ha_1_carry, ha_1_sum, ha_2_carry;

  ha ha_1 (.Sum(ha_1_sum), .Carry(ha_1_carry), .Ai(Bi), .Bi(Ai));
  ha ha_2 (.Sum(Sum), .Carry(ha_2_carry), .Ai(Carry_in), .Bi(ha_1_sum));
  or or_1 (Carry, ha_2_carry, ha_1_carry);
endmodule
