// Logisim project equality_detector.circ as structural Verilog: 2 circuits, main circuit 4 bit equality detector
module _4_bit_equality_detector (
  input  A0,
  input  B0,
  input  A1,
  input  B1,
  input  A2,
  input  B2,
  input  A3,
  input  B3,
  output out_9
);

  wire xnor_1_out, xnor_2_out, xnor_3_out, xnor_4_out;

  xnor xnor_1 (xnor_1_out, A0, B0);
  xnor xnor_2 (xnor_2_out, A1, B1);
  xnor xnor_3 (xnor_3_out, A2, B2);
  xnor xnor_4 (xnor_4_out, A3, B3);
  and and_1 (out_9, xnor_1_out, xnor_2_out, xnor_3_out, xnor_4_out);
endmodule

module _4_bit_magnitude_comparator (
  input  A0,
  input  B0,
  input  A1,
  input  B1,
  input  A2,
  input  B2,
  input  A3,
  input  B3,
  output A___B
);

  wire and_1_out, and_2_out, and_3_out, and_4_out, xnor_1_out, xnor_2_out, xnor_3_out;

  xnor xnor_1 (xnor_1_out, A1, B1);
  xnor xnor_2 (xnor_2_out, A2, B2);
  xnor xnor_3 (xnor_3_out, A3, B3);
  and and_1 (and_1_out, xnor_1_out, A0, xnor_2_out, xnor_3_out, ~B0);  // AND_Gate
  and and_2 (and_2_out, xnor_3_out, A1, xnor_2_out, ~B1);  // AND_Gate
  and and_3 (and_3_out, xnor_3_out, ~B2);  // AND_Gate
  and and_4 (and_4_out, A3, ~B3);  // AND_Gate
  or or_1 (A___B, and_1_out, and_2_out, and_3_out, and_4_out);
endmodule
