// Logisim project addition.circ as structural Verilog: 7 circuits, main circuit ha
module ripple_adder (
  input  A3,
  input  A2,
  input  A1,
  input  A0,
  input  B3,
  input  B2,
  input  B1,
  input  B0,
  output Carry_out,
  output D3,
  output D2,
  output D1,
  output D0
);

  wire full_adder_by_half_adder_2_carry, full_adder_by_half_adder_3_carry, ha_1_carry;

  full_adder_by_half_adder full_adder_by_half_adder_1 (
    .Ai(full_adder_by_half_adder_2_carry), .Bi(B3), .Carry_in(A3), .Sum(D3), .Carry(Carry_out));
  full_adder_by_half_adder full_adder_by_half_adder_2 (
    .Ai(full_adder_by_half_adder_3_carry), .Bi(B2), .Carry_in(A2), .Sum(D2),
    .Carry(full_adder_by_half_adder_2_carry));
  ha ha_1 (.Sum(D0), .Carry(ha_1_carry), .Ai(A0), .Bi(B0));
  full_adder_by_half_adder full_adder_by_half_adder_3 (
    .Ai(ha_1_carry), .Bi(B1), .Carry_in(A1), .Sum(D1), .Carry(full_adder_by_half_adder_3_carry));
endmodule

module full_adder (
  input  Ai,
  input  Bi,
  input  in_3,
  output Sum,
  output Carry
);

  wire and_1_out, and_2_out, or_1_out, xor_1_out;

  xor xor_1 (xor_1_out, Bi, Ai);
  or or_1 (or_1_out, Bi, Ai);
  xor xor_2 (Sum, xor_1_out, in_3);
  and and_1 (and_1_out, or_1_out, in_3);
  and and_2 (and_2_out, Bi, Ai);
  or or_2 (Carry, and_1_out, and_2_out);
endmodule

module full_adder_by_half_adder (
  input  Ai,
  input  Bi,
  input  Carry_in,
  output Sum,
  output Carry
);

  wire ha_1_carry, ha_1_sum, ha_2_carry;

  ha ha_1 (.Sum(ha_1_sum), .Carry(ha_1_carry), .Ai(Bi), .Bi(Ai));
  ha ha_2 (.Sum(Sum), .Carry(ha_2_carry), .Ai(Carry_in), .Bi(ha_1_sum));
  or or_1 (Carry, ha_2_carry, ha_1_carry);
endmodule

module ha (
  input  Ai,
  input  Bi,
  output Sum,
  output Carry
);

  xor xor_1 (Sum, Ai, Bi);
  and and_1 (Carry, Bi, Ai);
endmodule

module CLA (
  input  A1,
  input  A0,
  input  B1,
  input  B0,
  input  C0
);

  wire _0_g, _0_p, _1_g, _1_p, and_1_out, and_2_out, and_3_out, full_adder_by_half_adder_2_sum, or_1_out,
       or_2_out;

  and and_1 (and_1_out, _1_p, _0_g);
  and and_2 (and_2_out, _1_p, _0_p, C0);
  or or_1 (or_1_out, and_1_out, and_2_out, _1_g);
  p_and_g_calculator _1 (.A(B1), .B(A1), .P(_1_p), .G(_1_g));
  and and_3 (and_3_out, _0_p, C0);
  full_adder_by_half_adder full_adder_by_half_adder_1 (.Bi(B1), .Carry_in(or_2_out));  // open: Ai, Sum, Carry
  p_and_g_calculator _0 (.A(B0), .B(A0), .P(_0_p), .G(_0_g));
  or or_2 (or_2_out, and_3_out, _0_g);
  full_adder_by_half_adder full_adder_by_half_adder_2 (
    .Ai(A0), .Bi(B0), .Carry_in(C0), .Sum(full_adder_by_half_adder_2_sum));  // open: Carry
endmodule

module p_and_g_calculator (
  input  A,
  input  B,
  output P,
  output G
);

  xor xor_1 (P, B, A);
  and and_1 (G, B, A);
endmodule

module bcd_adder (
  input  B3,
  input  B2,
  input  B1,
  input  B0,
  input  A3,
  input  A2,
  input  A1,
  input  A0,
  output out_9,
  output out_10,
  output out_11,
  output out_12
);

  wire and_1_out, and_2_out, full_adder_by_half_adder_1_carry, full_adder_by_half_adder_1_sum,
       full_adder_by_half_adder_2_carry, full_adder_by_half_adder_2_sum, full_adder_by_half_adder_3_carry,
       full_adder_by_half_adder_3_sum, full_adder_by_half_adder_4_carry, full_adder_by_half_adder_5_carry,
       full_adder_by_half_adder_6_carry, or_1_out;

  and and_1 (and_1_out, full_adder_by_half_adder_1_sum, full_adder_by_half_adder_2_sum);
  and and_2 (and_2_out, full_adder_by_half_adder_1_sum, full_adder_by_half_adder_3_sum);
  or or_1 (or_1_out, full_adder_by_half_adder_1_carry, and_1_out, and_2_out);
  full_adder_by_half_adder full_adder_by_half_adder_1 (
    .Ai(A3), .Bi(B3), .Carry_in(full_adder_by_half_adder_2_carry), .Sum(full_adder_by_half_adder_1_sum),
    .Carry(full_adder_by_half_adder_1_carry));
  full_adder_by_half_adder full_adder_by_half_adder_2 (
    .Ai(A2), .Bi(B2), .Carry_in(full_adder_by_half_adder_3_carry), .Sum(full_adder_by_half_adder_2_sum),
    .Carry(full_adder_by_half_adder_2_carry));
  xor xor_1 (out_9, full_adder_by_half_adder_1_sum, full_adder_by_half_adder_6_carry);
  full_adder_by_half_adder full_adder_by_half_adder_3 (
    .Ai(A1), .Bi(B1), .Carry_in(full_adder_by_half_adder_4_carry), .Sum(full_adder_by_half_adder_3_sum),
    .Carry(full_adder_by_half_adder_3_carry));
  full_adder_by_half_adder full_adder_by_half_adder_4 (
    .Ai(A0), .Bi(B0), .Carry_in(1'b0), .Sum(out_12), .Carry(full_adder_by_half_adder_4_carry));
  full_adder_by_half_adder full_adder_by_half_adder_5 (
    .Ai(full_adder_by_half_adder_3_sum), .Bi(or_1_out), .Carry_in(1'b0), .Sum(out_11),
    .Carry(full_adder_by_half_adder_5_carry));
  full_adder_by_half_adder full_adder_by_half_adder_6 (
    .Ai(full_adder_by_half_adder_2_sum), .Bi(or_1_out), .Carry_in(full_adder_by_half_adder_5_carry),
    .Sum(out_10), .Carry(full_adder_by_half_adder_6_carry));
endmodule
