// Logisim project d-ff-with-async-control.circ as structural Verilog: 1 circuit, main circuit main
module main (
  input  Preset,
  input  Clear,
  input  D,
  input  Control
);

  wire nand_1_out, nand_2_out, nand_3_out, nand_4_out, nand_5_out, nand_6_out, nand_7_out, nand_8_out,
       not_1_out;

  nand nand_1 (nand_1_out, D, Control);
  nand nand_2 (nand_2_out, Control, ~D);  // NAND_Gate
  nand nand_3 (nand_3_out, nand_1_out, Preset, nand_4_out);
  not not_1 (not_1_out, Control);
  nand nand_4 (nand_4_out, nand_3_out, Clear, nand_2_out);
  nand nand_5 (nand_5_out, nand_3_out, not_1_out);
  nand nand_6 (nand_6_out, not_1_out, ~nand_3_out);  // NAND_Gate
  nand nand_7 (nand_7_out, nand_5_out, Preset, nand_8_out);
  nand nand_8 (nand_8_out, nand_7_out, Clear, nand_6_out);
endmodule
