// Logisim project mux.circ as structural Verilog: 1 circuit, main circuit main
module main (
  input  D,
  input  [2:0] A_B_C,
  output out_3
);

  wire not_1_out;

  not not_1 (not_1_out, D);
  Multiplexer #(.select(3)) multiplexer_1 (
    .in0(D), .in1(1'b1), .in2(not_1_out), .in3(1'b0), .in4(1'b0), .in5(1'b1), .in6(1'b0), .in7(1'b1),
    .out(out_3), .sel(A_B_C));  // open: en
endmodule
